// Logisim project ETFStudent.circ as structural Verilog: 10 circuits, main circuit REG32_LD
module REG32_LD (
  input  [31:0] I15__0,
  input  LD,
  input  mr,
  input  CLK,
  output [31:0] A15__0
);

  // REG16_LD reg16_ld_1: pin names not known; wires that end beside it: CLK, mr, I15__0[31:16], A15__0[31:16], LD
  // REG16_LD reg16_ld_2: pin names not known; wires that end beside it: CLK, mr, I15__0[15:0], A15__0[15:0], LD

  // Notes on the sheet:
  //   __
endmodule

module KMADR (
  input  immed,
  input  memdir,
  input  regdir,
  input  regindpom,
  output [3:0] Adr3__0
);

  assign Adr3__0 = immed ? 4'b0010 : 4'bz;  // Controlled_Buffer controlled_buffer_1
  assign Adr3__0 = memdir ? 4'b0100 : 4'bz;  // Controlled_Buffer controlled_buffer_2
  assign Adr3__0 = regdir ? 4'b0101 : 4'bz;  // Controlled_Buffer controlled_buffer_3
  assign Adr3__0 = regindpom ? 4'b0111 : 4'bz;  // Controlled_Buffer controlled_buffer_4
endmodule

module KMOPR (
  input  LD,
  input  ST,
  input  ADD,
  input  SUB,
  input  BLSS,
  input  JLEQ,
  input  JMP,
  input  JSR,
  input  RTS,
  input  RTI,
  input  HALT,
  output [5:0] Adr5__0
);

  assign Adr5__0 = LD ? 6'b000010 : 6'bz;  // Controlled_Buffer controlled_buffer_1
  assign Adr5__0 = ST ? 6'b000100 : 6'bz;  // Controlled_Buffer controlled_buffer_2
  assign Adr5__0 = ADD ? 6'b001010 : 6'bz;  // Controlled_Buffer controlled_buffer_3
  assign Adr5__0 = SUB ? 6'b001100 : 6'bz;  // Controlled_Buffer controlled_buffer_4
  assign Adr5__0 = BLSS ? 6'b001110 : 6'bz;  // Controlled_Buffer controlled_buffer_5
  assign Adr5__0 = JLEQ ? 6'b010000 : 6'bz;  // Controlled_Buffer controlled_buffer_6
  assign Adr5__0 = JMP ? 6'b010001 : 6'bz;  // Controlled_Buffer controlled_buffer_7
  assign Adr5__0 = JSR ? 6'b010010 : 6'bz;  // Controlled_Buffer controlled_buffer_8
  assign Adr5__0 = RTS ? 6'b010111 : 6'bz;  // Controlled_Buffer controlled_buffer_9
  assign Adr5__0 = RTI ? 6'b011110 : 6'bz;  // Controlled_Buffer controlled_buffer_10
  assign Adr5__0 = HALT ? 6'b100010 : 6'bz;  // Controlled_Buffer controlled_buffer_11
endmodule

module REG6_INC_LD (
  input  [5:0] I5__0,
  input  LD,
  input  INC,
  input  mr,
  input  CLK,
  output [5:0] A5__0
);

  wire reg2m_inc_ld_1_p7, reg2m_inc_ld_2_p8;

  // REG2m_INC_LD reg2m_inc_ld_1: pin names not known; wires that end beside it: CLK, mr, I5__0[5:4], A5__0[5:4], LD, INC, reg2m_inc_ld_1_p7
  // REG2m_INC_LD reg2m_inc_ld_2: pin names not known; wires that end beside it: CLK, reg2m_inc_ld_1_p7, mr, I5__0[3:2], A5__0[3:2], LD, INC, reg2m_inc_ld_2_p8
  // REG2m_INC_LD reg2m_inc_ld_3: pin names not known; wires that end beside it: CLK, reg2m_inc_ld_2_p8, mr, I5__0[1:0], A5__0[1:0], LD, INC, INC

  // Notes on the sheet:
  //   __
endmodule

module GPR16x16 (
  input  WR,
  input  CLK,
  input  [3:0] A3__0,
  input  [15:0] Din15__0,
  output [15:0] CLK_2
);

  wire gpr8x16_1_p5, gpr8x16_2_p5;

  // GPR8x16 gpr8x16_1: pin names not known; wires that end beside it: A3__0[2:0], CLK, Din15__0, CLK_2, gpr8x16_1_p5
  and and_1 (gpr8x16_1_p5, WR, A3__0[3]);
  // GPR8x16 gpr8x16_2: pin names not known; wires that end beside it: A3__0[2:0], CLK, Din15__0, CLK_2, gpr8x16_2_p5
  and and_2 (gpr8x16_2_p5, WR, A3__0[3]);

  // Other names for the same wires on the sheet: adr2__0[2:0] = A3__0[2:0]; adr3 = A3__0[3]
endmodule

module ALU16_add_inc_or_sub (
  input  [15:0] A,
  input  [15:0] B,
  input  \or ,
  input  add,
  input  inc,
  input  C0,
  input  sub,
  output [15:0] A_2,
  output c17,
  output eq
);

  wire C8sub, C17add, C17inc, C17sub, or_2_out;
  wire [7:0] sub8_1_p3;
  wire [15:0] ADD16__0, INC16__0, OR16, SUB16__0;

  assign OR16 = B | A;  // OR_Gate or_1, 16 bits wide
  // ADD16 add16_1: pin names not known; wires that end beside it: C17add, A, ADD16__0, B, C0
  // SUB16 sub16_1: pin names not known; wires that end beside it: C17sub, A, SUB16__0, B, C0
  // SUB8 sub8_1: pin names not known; wires that end beside it: C8sub, A[7:0], sub8_1_p3, B[7:0], 1'b0
  // INC16 inc16_1: pin names not known; wires that end beside it: C17inc, B, INC16__0, 1'b1
  or or_2 (or_2_out, sub8_1_p3[0], sub8_1_p3[1], sub8_1_p3[2], sub8_1_p3[3], sub8_1_p3[4], sub8_1_p3[5], sub8_1_p3[6], sub8_1_p3[7]);
  not not_1 (eq, or_2_out);
  assign A_2 = \or  ? OR16 : 16'bz;  // Controlled_Buffer controlled_buffer_1
  assign A_2 = inc ? INC16__0 : 16'bz;  // Controlled_Buffer controlled_buffer_2
  assign A_2 = add ? ADD16__0 : 16'bz;  // Controlled_Buffer controlled_buffer_3
  assign A_2 = sub ? SUB16__0 : 16'bz;  // Controlled_Buffer controlled_buffer_4
  assign c17 = inc ? C17inc : 1'bz;  // Controlled_Buffer controlled_buffer_5
  assign c17 = add ? C17add : 1'bz;  // Controlled_Buffer controlled_buffer_6
  assign c17 = sub ? C17sub : 1'bz;  // Controlled_Buffer controlled_buffer_7
  Pull_Resistor pull_resistor_1 (.node(c17));
  Pull_Resistor pull_resistor_2 (.node(A_2));

  // Other names for the same wires on the sheet: A7__0[7:0] = A[7:0]; A15__0[15:0] = A; A15__8[7:0] = A[15:8];
  //   B7__0[7:0] = B[7:0]; B15__0[15:0] = B; B15__8[7:0] = B[15:8]
endmodule

module ROM_EXEC (
  input  [7:0] A8__0,
  input  CS,
  output [7:0] DOUT51__44,
  output [11:0] DOUT11__0,
  output [31:0] DOUT43__12
);

  ROM rom_1 (.addr(A8__0), .data(DOUT51__44), .sel(CS));
  ROM #(.dataWidth(32)) rom_2 (.addr(A8__0), .data(DOUT43__12), .sel(CS));
  ROM #(.dataWidth(12)) rom_3 (.addr(A8__0), .data(DOUT11__0), .sel(CS));

  // Other names for the same wires on the sheet: A[7:0] = A8__0

  // Notes on the sheet:
  //   contents of rom_1 (hex, n*v repeats v):
  //   0 0 44 0 0 5 0 7 0 0 0 b 0 d 0 44 0 44 0 44 0 15 0 17 44 0 0 1b 0 1d 12*44 0 2b 0 2d 44
endmodule

module KMOPR_EXEC (
  input  prazna,
  input  grinst,
  input  STRFIND,
  input  OR,
  input  INC,
  input  ADD,
  input  ST,
  input  LD,
  input  JSR,
  input  JMP,
  input  JLEQ,
  input  BGRT,
  input  BNNG,
  input  BGREU,
  input  BLEQ,
  input  POP,
  input  PUSH,
  input  RORC,
  input  ROR,
  input  RTS,
  input  RTI,
  input  HALT,
  output [7:0] Adr7__0
);

  assign Adr7__0 = prazna ? {8{1'b0}} : 8'bz;  // Controlled_Buffer controlled_buffer_1
  assign Adr7__0 = grinst ? 8'h44 : 8'bz;  // Controlled_Buffer controlled_buffer_2
  assign Adr7__0 = STRFIND ? 8'h3f : 8'bz;  // Controlled_Buffer controlled_buffer_3
  assign Adr7__0 = OR ? 8'h3d : 8'bz;  // Controlled_Buffer controlled_buffer_4
  assign Adr7__0 = INC ? 8'h3b : 8'bz;  // Controlled_Buffer controlled_buffer_5
  assign Adr7__0 = ADD ? 8'h39 : 8'bz;  // Controlled_Buffer controlled_buffer_6
  assign Adr7__0 = ST ? 8'h31 : 8'bz;  // Controlled_Buffer controlled_buffer_7
  assign Adr7__0 = LD ? 8'h2f : 8'bz;  // Controlled_Buffer controlled_buffer_8
  assign Adr7__0 = JSR ? 8'h2a : 8'bz;  // Controlled_Buffer controlled_buffer_9
  assign Adr7__0 = JMP ? 8'h29 : 8'bz;  // Controlled_Buffer controlled_buffer_10
  assign Adr7__0 = JLEQ ? 8'h27 : 8'bz;  // Controlled_Buffer controlled_buffer_11
  assign Adr7__0 = BNNG ? 8'h23 : 8'bz;  // Controlled_Buffer controlled_buffer_12
  assign Adr7__0 = BGRT ? 8'h25 : 8'bz;  // Controlled_Buffer controlled_buffer_13
  assign Adr7__0 = BGREU ? 8'h21 : 8'bz;  // Controlled_Buffer controlled_buffer_14
  assign Adr7__0 = BLEQ ? 8'h1f : 8'bz;  // Controlled_Buffer controlled_buffer_15
  assign Adr7__0 = PUSH ? 8'h14 : 8'bz;  // Controlled_Buffer controlled_buffer_16
  assign Adr7__0 = POP ? 8'h19 : 8'bz;  // Controlled_Buffer controlled_buffer_17
  assign Adr7__0 = RORC ? 8'h12 : 8'bz;  // Controlled_Buffer controlled_buffer_18
  assign Adr7__0 = ROR ? 8'h10 : 8'bz;  // Controlled_Buffer controlled_buffer_19
  assign Adr7__0 = RTS ? 8'h9 : 8'bz;  // Controlled_Buffer controlled_buffer_20
  assign Adr7__0 = RTI ? 8'h3 : 8'bz;  // Controlled_Buffer controlled_buffer_21
  assign Adr7__0 = HALT ? 8'h2 : 8'bz;  // Controlled_Buffer controlled_buffer_22
endmodule

module KMOPR_ADDR (
  input  prazna,
  input  regdir,
  input  postdec,
  input  postincr,
  input  regind,
  input  memind,
  input  memdir,
  input  immed,
  output [5:0] Adr5__0
);

  assign Adr5__0 = prazna ? {6{1'b0}} : 6'bz;  // Controlled_Buffer controlled_buffer_1
  assign Adr5__0 = regdir ? 6'b010010 : 6'bz;  // Controlled_Buffer controlled_buffer_2
  assign Adr5__0 = postdec ? 6'b001111 : 6'bz;  // Controlled_Buffer controlled_buffer_3
  assign Adr5__0 = postincr ? 6'b001100 : 6'bz;  // Controlled_Buffer controlled_buffer_4
  assign Adr5__0 = regind ? 6'b001011 : 6'bz;  // Controlled_Buffer controlled_buffer_5
  assign Adr5__0 = memind ? 6'b000101 : 6'bz;  // Controlled_Buffer controlled_buffer_6
  assign Adr5__0 = memdir ? 6'b000100 : 6'bz;  // Controlled_Buffer controlled_buffer_7
  assign Adr5__0 = immed ? 6'b000010 : 6'bz;  // Controlled_Buffer controlled_buffer_8
endmodule

module ROM64FETCH (
  input  [5:0] A5__0,
  input  CS,
  output [30:0] DOUT30__0,
  output [5:0] DOUT36__31
);

  ROM #(.addrWidth(6), .dataWidth(6)) rom_1 (.addr(A5__0), .data(DOUT36__31), .sel(CS));
  ROM #(.addrWidth(6), .dataWidth(31)) rom_2 (.addr(A5__0), .data(DOUT30__0), .sel(CS));
endmodule
