// Logisim project ORT2Project_Aleksa.circ as structural Verilog: 8 circuits, main circuit COMPUTER
module COMPUTER (
);

  wire BTN_RST_out, CLK, cpu_1_inta, interrupt_interface_4_1_p4, interrupt_interface_4_1_p5,
       interrupt_interface_4_1_p6, interrupt_interface_4_1_p7, pull_resistor_1_node, pull_resistor_5_node,
       ram_1_out_8, rst;
  wire [1:0] cpu_1_uext1__0;
  wire [3:0] interrupt_interface_4_1_p1;
  wire [7:0] pull_resistor_4_node, ram_1_out_7;
  wire [15:0] pull_resistor_2_node;

  Button BTN_RST (.out(BTN_RST_out));
  Clock u_CLK (.out(CLK));
  // RisingEdge risingedge_1: pin names not known; wires that end beside it: BTN_RST_out, CLK, rst
  RAM ram_1 (
    .in_1(pull_resistor_2_node), .in_2(CLK), .in_3(pull_resistor_4_node), .in_4(pull_resistor_1_node),
    .in_5(pull_resistor_5_node), .in_6(rst), .out_7(ram_1_out_7), .out_8(ram_1_out_8));
  Pull_Resistor pull_resistor_1 (.node(pull_resistor_1_node));
  Pull_Resistor pull_resistor_2 (.node(pull_resistor_2_node));
  Pull_Resistor pull_resistor_3 (.node(ram_1_out_7));
  Pull_Resistor pull_resistor_4 (.node(pull_resistor_4_node));
  Pull_Resistor pull_resistor_5 (.node(pull_resistor_5_node));
  Pull_Resistor pull_resistor_6 (.node(ram_1_out_8));
  CPU cpu_1 (
    .in_1(rst), .in_2(CLK), .in_3(ram_1_out_8), .in_4(ram_1_out_7), .ABUS(pull_resistor_2_node),
    .DOUTBUS(pull_resistor_4_node), .out_8(pull_resistor_1_node), .out_9(pull_resistor_5_node),
    .inta(cpu_1_inta), .intr3__0(interrupt_interface_4_1_p1), .UEXT1__0(cpu_1_uext1__0));
  // INTERRUPT_INTERFACE_4 interrupt_interface_4_1: pin names not known; wires that end beside it: interrupt_interface_4_1_p1, cpu_1_inta, cpu_1_uext1__0, interrupt_interface_4_1_p4, interrupt_interface_4_1_p5, interrupt_interface_4_1_p6, interrupt_interface_4_1_p7, CLK
  Button BTN_INTR3 (.out(interrupt_interface_4_1_p4));
  Button BTN_INTR2 (.out(interrupt_interface_4_1_p5));
  Button BTN_INTR1 (.out(interrupt_interface_4_1_p6));
  Button BTN_INTR0 (.out(interrupt_interface_4_1_p7));
endmodule

module CPU (
  input  in_1,
  input  in_2,
  input  in_3,
  input  [7:0] in_4,
  input  [3:0] intr3__0,
  output [15:0] ABUS,
  output [7:0] DOUTBUS,
  output out_8,
  output out_9,
  output inta,
  output [1:0] UEXT1__0
);

  wire [3:0] common_1_addrbus, common_1_phaseffbus;
  wire [5:0] pull_resistor_1_node;
  wire [7:0] A, ALU, B, PSW, pull_resistor_7_node;
  wire [8:0] pull_resistor_4_node;
  wire [10:0] common_1_instrucbus;
  wire [14:0] pull_resistor_6_node;
  wire [15:0] INTRADDR;

  COMMON common_1 (
    .CLK(in_2), .RST(in_1), .DIN(in_4), .CMEMBUS(pull_resistor_6_node), .MAR(ABUS), .MDR(DOUTBUS),
    .PHASEFFBUS(common_1_phaseffbus), .INSTRUCBUS(common_1_instrucbus), .ADDRBUS(common_1_addrbus),
    .PSWL(PSW), .CREGBUS(pull_resistor_4_node), .CFFBUS(pull_resistor_7_node), .B(B), .A(A),
    .CPSW(pull_resistor_1_node), .ALU(ALU), .IVTPPDSP(INTRADDR));  // open: PSWH
  Pull_Resistor pull_resistor_1 (.node(pull_resistor_1_node));
  Pull_Resistor pull_resistor_2 (.node(common_1_instrucbus));
  Pull_Resistor pull_resistor_3 (.node(common_1_phaseffbus));
  Pull_Resistor pull_resistor_4 (.node(pull_resistor_4_node));
  Pull_Resistor pull_resistor_5 (.node(common_1_addrbus));
  Pull_Resistor pull_resistor_6 (.node(pull_resistor_6_node));
  Pull_Resistor pull_resistor_7 (.node(pull_resistor_7_node));
  FETCH fetch_1 (
    .in_1(in_1), .in_2(in_2), .in_3(in_3), .PHASEFFBUS(common_1_phaseffbus),
    .INSTRUCBUS(common_1_instrucbus), .ADDRBUS(common_1_addrbus), .PSW(PSW), .rdMEM(out_9),
    .CMEMBUS(pull_resistor_6_node), .CFFBUS(pull_resistor_7_node), .CREGBUS(pull_resistor_4_node));
  ADDR addr_1 (
    .in_1(in_1), .in_2(in_2), .in_3(in_3), .PHASEFFBUS(common_1_phaseffbus),
    .INSTRUCBUS(common_1_instrucbus), .ADDRBUS(common_1_addrbus), .rdMEM(out_9),
    .CMEMBUS(pull_resistor_6_node), .CFFBUS(pull_resistor_7_node), .CREGBUS(pull_resistor_4_node));
  EXEC exec_1 (
    .in_1(in_1), .in_2(in_2), .in_3(in_3), .B(B), .PHASEFFBUS(common_1_phaseffbus),
    .INSTRUCBUS(common_1_instrucbus), .ADDRBUS(common_1_addrbus), .PSW(PSW), .A(A), .ALU(ALU),
    .CMEMBUS(pull_resistor_6_node), .CFFBUS(pull_resistor_7_node), .CREGBUS(pull_resistor_4_node),
    .CPSW(pull_resistor_1_node), .rdMEM(out_9), .wrMEM(out_8));
  INTR intr_1 (
    .in_1(in_1), .in_2(in_2), .in_3(in_3), .PHASEFFBUS(common_1_phaseffbus),
    .INSTRUCBUS(common_1_instrucbus), .PSW(PSW), .intr(intr3__0), .ADDIVTP(INTRADDR),
    .CMEMBUS(pull_resistor_6_node), .CFFBUS(pull_resistor_7_node), .CREGBUS(pull_resistor_4_node),
    .rdMEM(out_9), .wrMEM(out_8), .UEXT1__0(UEXT1__0), .inta(inta));

  // Other names for the same wires on the sheet: CLK = in_2; DIN7__0[7:0] = in_4; FCBUS = in_3; MAR[15:0] = ABUS;
  //   MDR[7:0] = DOUTBUS; RD = out_9; rst = in_1; WR = out_8
endmodule

module COMMON (
  input  CLK,
  input  RST,
  input  [7:0] DIN,
  input  [7:0] A,
  input  [7:0] ALU,
  input  [15:0] IVTPPDSP,
  input  [14:0] CMEMBUS,
  input  [7:0] CFFBUS,
  input  [8:0] CREGBUS,
  input  [5:0] CPSW,
  output [15:0] MAR,
  output [7:0] MDR,
  output [3:0] PHASEFFBUS,
  output [10:0] INSTRUCBUS,
  output [3:0] ADDRBUS,
  output [7:0] PSWL,
  output [7:0] PSWH,
  output [7:0] B
);

  wire and_1_out, and_2_out, and_3_out, and_4_out, and_5_out, and_6_out, and_7_out, and_8_out, and_9_out,
       and_10_out, and_11_out, and_12_out, and_13_out, and_14_out, and_15_out, and_16_out, and_17_out,
       and_18_out, and_19_out, and_20_out, C, clPSWI, ldC, ldIR31__24, ldN, ldPSWH, ldPSWL, ldV, ldZ, MDR0,
       MDR1, MDR2, MDR3, MDR4, MDR15, mp2_16b_1_p3, N, not_1_out, not_3_out, not_4_out, not_5_out, not_6_out,
       not_7_out, not_9_out, not_11_out, not_12_out, not_13_out, not_14_out, not_15_out, or_2_out, or_3_out,
       or_4_out, or_5_out, or_6_out, or_7_out, or_8_out, or_9_out, or_10_out, or_11_out, or_12_out,
       or_13_out, reg16_inc_ld_2_p4, rsff_2_p4, rsff_3_p4, rsff_6_p4, stPSWI, stPSWSTART, V, Z;
  wire [7:0] IR7__0, IR15__8, IR23__16, IR31__24;
  wire [15:0] inPC, PC15__0;

  // REG16_INC_LD reg16_inc_ld_1: pin names not known; wires that end beside it: CLK, PC15__0, MAR, CMEMBUS[0], CMEMBUS[1]
  // REG8_LD reg8_ld_1: pin names not known; wires that end beside it: CLK, MDR, IR31__24, ldIR31__24
  // REG8_LD reg8_ld_2: pin names not known; wires that end beside it: CLK, MDR, IR23__16, CREGBUS[6]
  // REG8_LD reg8_ld_3: pin names not known; wires that end beside it: CLK, DIN, MDR, CMEMBUS[2]
  // REG8_LD reg8_ld_4: pin names not known; wires that end beside it: CLK, MDR, IR15__8, CREGBUS[5]
  // REG8_LD reg8_ld_5: pin names not known; wires that end beside it: CLK, MDR, IR7__0, CREGBUS[4]
  not not_1 (not_1_out, RST);
  // RSFF rsff_1: pin names not known; wires that end beside it: CFFBUS[1], CLK, CFFBUS[0], not_1_out, PHASEFFBUS[0]
  // MP2_16b mp2_16b_1: pin names not known; wires that end beside it: RST, inPC, mp2_16b_1_p3, 16'h1000, 1'b1
  // REG16_INC_LD reg16_inc_ld_2: pin names not known; wires that end beside it: CLK, mp2_16b_1_p3, PC15__0, reg16_inc_ld_2_p4, CMEMBUS[4]
  or or_1 (reg16_inc_ld_2_p4, CMEMBUS[3], RST);
  // RSFF rsff_2: pin names not known; wires that end beside it: CFFBUS[3], CLK, CFFBUS[2], rsff_2_p4, PHASEFFBUS[1]
  not not_2 (rsff_2_p4, RST);
  not not_3 (not_3_out, C);
  not not_4 (not_4_out, V);
  not not_5 (not_5_out, N);
  not not_6 (not_6_out, MDR15);
  and and_1 (and_1_out, ldC, C);
  and and_2 (and_2_out, ldC, not_3_out);
  and and_3 (and_3_out, ldV, V);
  and and_4 (and_4_out, ldV, not_4_out);
  and and_5 (and_5_out, ldN, N);
  and and_6 (and_6_out, ldN, not_5_out);
  and and_7 (and_7_out, ldZ, Z);
  and and_8 (and_8_out, ldZ, not_7_out);
  not not_7 (not_7_out, Z);
  // RSFF rsff_3: pin names not known; wires that end beside it: CFFBUS[5], CLK, CFFBUS[4], rsff_3_p4, PHASEFFBUS[2]
  not not_8 (rsff_3_p4, RST);
  or or_2 (or_2_out, stPSWI, and_9_out);
  and and_9 (and_9_out, ldPSWH, MDR15);
  and and_10 (and_10_out, ldPSWH, not_6_out);
  or or_3 (or_3_out, and_10_out, clPSWI);
  and and_11 (and_11_out, ldPSWL, MDR0);
  and and_12 (and_12_out, ldPSWL, not_9_out);
  not not_9 (not_9_out, MDR0);
  // RSFF rsff_4: pin names not known; wires that end beside it: or_2_out, CLK, or_3_out, PSWH[7]
  // NOT_Gate not_10 has open pins: in=RST, out=open
  and and_13 (and_13_out, ldPSWL, MDR4);
  and and_14 (and_14_out, ldPSWL, not_11_out);
  not not_11 (not_11_out, MDR4);
  and and_15 (and_15_out, ldPSWL, MDR3);
  and and_16 (and_16_out, ldPSWL, not_12_out);
  not not_12 (not_12_out, MDR3);
  and and_17 (and_17_out, ldPSWL, MDR2);
  and and_18 (and_18_out, ldPSWL, not_13_out);
  not not_13 (not_13_out, MDR2);
  not not_14 (not_14_out, MDR1);
  or or_4 (or_4_out, stPSWSTART, and_11_out);
  or or_5 (or_5_out, and_12_out, CPSW[0]);
  or or_6 (or_6_out, and_1_out, and_13_out);
  or or_7 (or_7_out, and_14_out, and_2_out);
  or or_8 (or_8_out, and_3_out, and_15_out);
  or or_9 (or_9_out, and_16_out, and_4_out);
  or or_10 (or_10_out, and_5_out, and_17_out);
  or or_11 (or_11_out, and_18_out, and_6_out);
  or or_12 (or_12_out, and_7_out, and_19_out);
  and and_19 (and_19_out, ldPSWL, MDR1);
  and and_20 (and_20_out, ldPSWL, not_14_out);
  or or_13 (or_13_out, and_20_out, and_8_out);
  not not_15 (not_15_out, RST);
  // RSFF rsff_5: pin names not known; wires that end beside it: or_4_out, CLK, or_5_out, not_15_out, PSWL[0]
  // RSFF rsff_6: pin names not known; wires that end beside it: CFFBUS[7], CLK, CFFBUS[6], rsff_6_p4, PHASEFFBUS[3]
  not not_16 (rsff_6_p4, RST);
  // RSFF rsff_7: pin names not known; wires that end beside it: or_6_out, CLK, or_7_out, PSWL[4]
  // NOT_Gate not_17 has open pins: in=RST, out=open
  // RSFF rsff_8: pin names not known; wires that end beside it: or_8_out, CLK, or_9_out, PSWL[3]
  // NOT_Gate not_18 has open pins: in=RST, out=open
  // RSFF rsff_9: pin names not known; wires that end beside it: or_10_out, CLK, or_11_out, PSWL[2]
  // NOT_Gate not_19 has open pins: in=RST, out=open
  // RSFF rsff_10: pin names not known; wires that end beside it: or_12_out, CLK, or_13_out, PSWL[1]
  // NOT_Gate not_20 has open pins: in=RST, out=open

  assign PSWH[6:0] = {7{1'b0}};
  assign PSWL[7:5] = 3'b000;

  // Other names for the same wires on the sheet: A7__0[7:0] = A; ALU7__0[7:0] = ALU; B7__0[7:0] = B;
  //   stFETCH = CFFBUS[0]; clFETCH = CFFBUS[1]; stADDR = CFFBUS[2]; clADDR = CFFBUS[3]; stEXEC = CFFBUS[4];
  //   clEXEC = CFFBUS[5]; stINTR = CFFBUS[6]; clINTR = CFFBUS[7]; ldMAR = CMEMBUS[0]; incMAR = CMEMBUS[1];
  //   ldMDR = CMEMBUS[2]; ldPC = CMEMBUS[3]; incPC = CMEMBUS[4]; clPSWSTART = CPSW[0]; ldIR7__0 = CREGBUS[4];
  //   ldIR15__8 = CREGBUS[5]; ldIR23__16 = CREGBUS[6]; Din7__0[7:0] = DIN; ENTRADDR15__0[15:0] = IVTPPDSP;
  //   MAR15__0[15:0] = MAR; MDR7__0[7:0] = MDR; FETCH = PHASEFFBUS[0]; ADDR = PHASEFFBUS[1]; EXEC = PHASEFFBUS[2];
  //   INTR = PHASEFFBUS[3]; PSW7__0[4:0] = PSWL[4:0]; PSWSTART = PSWL[0]; PSWZ = PSWL[1]; PSWN = PSWL[2];
  //   PSWV = PSWL[3]; PSWC = PSWL[4]; PSW15__8[7] = PSWH[7]; PSWI = PSWH[7]

  // Notes on the sheet:
  //   Instrukcijski registar
  //   MAR
  //   Dekoderi za prepoznavanje instrukcije na osnovu sadrzaja registra IR23..16
  //   MDR
  //   PC
  //   FF za pokretanje FETCH, ADDR, EXEC i INTR faze izvršavanja instrukcije
  //   Programska statusna reč (PSW)
endmodule

module FETCH (
  input  in_1,
  input  in_2,
  input  in_3,
  input  [3:0] PHASEFFBUS,
  input  [10:0] INSTRUCBUS,
  input  [3:0] ADDRBUS,
  input  [7:0] PSW,
  output [14:0] CMEMBUS,
  output [7:0] CFFBUS,
  output [8:0] CREGBUS,
  output rdMEM
);

  wire ADD, adr2, adr4, bezadr1, BGREU, BGRT, BLEQ, BNNG, HALT, immed, INC, JLEQ, JMP, jmp2, jmp3, JSR, LD,
       memdir, memind, OR, or_4_out, or_5_out, or_6_out, or_7_out, POP, postdec, postincr, PUSH, regdir,
       regind, ROR, RORC, RTI, RTS, ST, STRFIND;

  or or_1 (bezadr1, HALT, RTS, RTI, ROR, RORC, PUSH, POP);
  or or_2 (jmp3, JLEQ, JMP, JSR);
  or or_3 (jmp2, BLEQ, BGREU, BNNG, BGRT);
  or or_4 (or_4_out, LD, ST, ADD, INC, OR, STRFIND);
  or or_5 (or_5_out, regind, postincr, postdec, regdir);
  and and_1 (adr2, or_4_out, or_5_out);
  or or_6 (or_6_out, LD, ST, ADD, INC, OR, STRFIND);
  or or_7 (or_7_out, immed, memdir, memind);
  and and_2 (adr4, or_6_out, or_7_out);

  // Other names for the same wires on the sheet: CLK = in_2; FCBUS = in_3; rst = in_1

  // Notes on the sheet:
  //   Operaciona jedinica
  //   Kontrolna jedinica
endmodule

module ADDR (
  input  in_1,
  input  in_2,
  input  in_3,
  input  [3:0] PHASEFFBUS,
  input  [10:0] INSTRUCBUS,
  input  [3:0] ADDRBUS,
  output [14:0] CMEMBUS,
  output [7:0] CFFBUS,
  output [8:0] CREGBUS,
  output rdMEM
);


  // Other names for the same wires on the sheet: CLK = in_2; FCBUS = in_3; rst = in_1

  // Notes on the sheet:
  //   Operaciona jedinica
  //   Upravljacka jedinica
endmodule

module EXEC (
  input  in_1,
  input  in_2,
  input  in_3,
  input  [7:0] B,
  input  [3:0] PHASEFFBUS,
  input  [10:0] INSTRUCBUS,
  input  [3:0] ADDRBUS,
  input  [7:0] PSW,
  output [7:0] A,
  output [7:0] ALU,
  output [14:0] CMEMBUS,
  output [7:0] CFFBUS,
  output [8:0] CREGBUS,
  output [5:0] CPSW,
  output rdMEM,
  output wrMEM
);


  // Other names for the same wires on the sheet: A7__0[7:0] = A; ALU7__0[7:0] = ALU; B7__0[7:0] = B; CLK = in_2;
  //   FCBUS = in_3; rst = in_1

  // Notes on the sheet:
  //   Operaciona jedinica
  //   Upravljacka jedinica
endmodule

module INTR (
  input  in_1,
  input  in_2,
  input  in_3,
  input  [3:0] PHASEFFBUS,
  input  [10:0] INSTRUCBUS,
  input  [7:0] PSW,
  input  [3:0] intr,
  output [15:0] ADDIVTP,
  output [1:0] UEXT1__0,
  output inta,
  output [14:0] CMEMBUS,
  output [7:0] CFFBUS,
  output [8:0] CREGBUS,
  output rdMEM,
  output wrMEM
);


  // Other names for the same wires on the sheet: ADDIVTP15__0[15:0] = ADDIVTP; CLK = in_2; FCBUS = in_3;
  //   intr3__0[3:0] = intr; ldBR = inta; rst = in_1

  // Notes on the sheet:
  //   Operaciona jedinica
  //   Upravljacka jedinica
endmodule

module RAM (
  input  [15:0] in_1,
  input  in_2,
  input  [7:0] in_3,
  input  in_4,
  input  in_5,
  input  in_6,
  output [7:0] out_7,
  output out_8
);

  wire and_1_out, and_2_out, CNT0, LDCNT, not_1_out, notCNT0, or_1_out, reg4_ld_sl_sr_1_p6, rsff_2_p4,
       rsff_2_p5, rsff_3_p4, sl;
  wire [3:0] CNT, LFSR;

  // RSFF rsff_1: pin names not known; wires that end beside it: 1'b0, in_2, in_6, sl
  or or_1 (or_1_out, in_4, in_5);
  // REG4_LD_SL_SR reg4_ld_sl_sr_1: pin names not known; wires that end beside it: 1'b0, 1'b0, in_2, 4'b1111, LFSR, reg4_ld_sl_sr_1_p6, sl, in_6
  // RisingEdge risingedge_1: pin names not known; wires that end beside it: or_1_out, in_2, LDCNT
  // MEM64Kx8 mem64kx8_1: pin names not known; wires that end beside it: in_1, 1'b1, in_2, in_3, out_7, in_4
  xor xor_1 (reg4_ld_sl_sr_1_p6, LFSR[2], LFSR[3]);
  and and_1 (and_1_out, CNT0, not_1_out);
  not not_1 (not_1_out, LDCNT);
  // RSFF rsff_2: pin names not known; wires that end beside it: and_1_out, in_2, LDCNT, rsff_2_p4, rsff_2_p5
  not not_2 (rsff_2_p4, in_6);
  and and_2 (and_2_out, rsff_2_p5, CNT0);
  // REG4m_DEC_LD reg4m_dec_ld_1: pin names not known; wires that end beside it: in_2, LFSR, CNT, LDCNT, notCNT0, notCNT0
  or or_2 (notCNT0, CNT[0], CNT[1], CNT[2], CNT[3]);
  // RSFF rsff_3: pin names not known; wires that end beside it: out_8, in_2, and_2_out, rsff_3_p4, out_8
  not not_3 (rsff_3_p4, in_6);
  not not_4 (CNT0, notCNT0);

  // Other names for the same wires on the sheet: ADR[15:0] = in_1; CLK = in_2; DIN[7:0] = in_3; DOUT[7:0] = out_7;
  //   fc = out_8; RDMEM = in_5; rst = in_6; WRMEM = in_4

  // Notes on the sheet:
  //   Random broj predstavlja vreme pristupa memoriji
  //   Brojac za generisanje random broja 
  //   Jedinica za generisanje function complete (fc) signala
  //   Brojac za dekrementiranje random broja
endmodule
