// Logisim project ORT2Project_Zavrsen.circ as structural Verilog: 8 circuits, main circuit COMPUTER
module COMPUTER (
);

  wire BTN_RST_out, CLK, cpu_1_inta, interrupt_interface_4_1_p4, interrupt_interface_4_1_p5,
       interrupt_interface_4_1_p6, interrupt_interface_4_1_p7, pull_resistor_1_node, pull_resistor_5_node,
       ram_1_out_8, rst;
  wire [1:0] cpu_1_uext1__0;
  wire [3:0] interrupt_interface_4_1_p1;
  wire [7:0] pull_resistor_4_node, ram_1_out_7;
  wire [15:0] pull_resistor_3_node;

  Button BTN_RST (.out(BTN_RST_out));
  Clock u_CLK (.out(CLK));
  // RisingEdge risingedge_1: pin names not known; wires that end beside it: BTN_RST_out, CLK, rst
  RAM ram_1 (
    .in_1(pull_resistor_3_node), .in_2(CLK), .in_3(pull_resistor_4_node), .in_4(pull_resistor_1_node),
    .in_5(pull_resistor_5_node), .in_6(rst), .out_7(ram_1_out_7), .out_8(ram_1_out_8));
  Pull_Resistor pull_resistor_1 (.node(pull_resistor_1_node));
  Pull_Resistor pull_resistor_2 (.node(ram_1_out_7));
  Pull_Resistor pull_resistor_3 (.node(pull_resistor_3_node));
  Pull_Resistor pull_resistor_4 (.node(pull_resistor_4_node));
  Pull_Resistor pull_resistor_5 (.node(pull_resistor_5_node));
  Pull_Resistor pull_resistor_6 (.node(ram_1_out_8));
  CPU cpu_1 (
    .in_1(rst), .in_2(CLK), .in_3(ram_1_out_8), .in_4(ram_1_out_7), .ABUS(pull_resistor_3_node),
    .DOUTBUS(pull_resistor_4_node), .out_8(pull_resistor_1_node), .out_9(pull_resistor_5_node),
    .inta(cpu_1_inta), .intr3__0(interrupt_interface_4_1_p1), .UEXT1__0(cpu_1_uext1__0));
  // INTERRUPT_INTERFACE_4 interrupt_interface_4_1: pin names not known; wires that end beside it: interrupt_interface_4_1_p1, cpu_1_inta, cpu_1_uext1__0, interrupt_interface_4_1_p4, interrupt_interface_4_1_p5, interrupt_interface_4_1_p6, interrupt_interface_4_1_p7, CLK
  Button BTN_INTR3 (.out(interrupt_interface_4_1_p4));
  Button BTN_INTR2 (.out(interrupt_interface_4_1_p5));
  Button BTN_INTR1 (.out(interrupt_interface_4_1_p6));
  Button BTN_INTR0 (.out(interrupt_interface_4_1_p7));
endmodule

module CPU (
  input  in_1,
  input  in_2,
  input  in_3,
  input  [7:0] in_4,
  input  [3:0] intr3__0,
  output [15:0] ABUS,
  output [7:0] DOUTBUS,
  output out_8,
  output out_9,
  output inta,
  output [1:0] UEXT1__0
);

  wire [3:0] common_1_instadrout, common_1_out_13;
  wire [5:0] pull_resistor_1_node;
  wire [7:0] A, ALU, B, PSW;
  wire [9:0] pull_resistor_7_node;
  wire [10:0] common_1_instout;
  wire [15:0] INTRADDR;
  wire [23:0] pull_resistor_4_node, pull_resistor_6_node;

  COMMON common_1 (
    .CLK(in_2), .RST(in_1), .DIN(in_4), .CMEMBUS(pull_resistor_4_node), .MAR(ABUS), .MDR(DOUTBUS),
    .out_13(common_1_out_13), .INSTOUT(common_1_instout), .INSTADROUT(common_1_instadrout), .PSW(PSW),
    .CREGBUS(pull_resistor_6_node), .CFFBUS(pull_resistor_7_node), .B(B), .A(A), .CPSW(pull_resistor_1_node),
    .ALU(ALU), .IVTPPDSP(INTRADDR));
  Pull_Resistor pull_resistor_1 (.node(pull_resistor_1_node));
  Pull_Resistor pull_resistor_2 (.node(common_1_out_13));
  Pull_Resistor pull_resistor_3 (.node(common_1_instout));
  Pull_Resistor pull_resistor_4 (.node(pull_resistor_4_node));
  Pull_Resistor pull_resistor_5 (.node(common_1_instadrout));
  Pull_Resistor pull_resistor_6 (.node(pull_resistor_6_node));
  Pull_Resistor pull_resistor_7 (.node(pull_resistor_7_node));
  FETCH fetch_1 (
    .in_1(in_1), .in_2(in_2), .in_3(in_3), .in_4(common_1_out_13), .in_5(common_1_instout),
    .in_6(common_1_instadrout), .PSW(PSW), .out_11(out_9), .CMEMBUS(pull_resistor_4_node),
    .CFFBUS(pull_resistor_7_node), .CREGBUS(pull_resistor_6_node));
  ADDR addr_1 (
    .in_1(in_1), .in_2(in_2), .in_3(in_3), .in_4(common_1_out_13), .in_5(common_1_instout),
    .in_6(common_1_instadrout), .out_10(out_9), .CMEMBUS(pull_resistor_4_node),
    .CFFBUS(pull_resistor_7_node), .CREGBUS(pull_resistor_6_node));
  EXEC exec_1 (
    .in_1(in_1), .in_2(in_2), .in_3(in_3), .B(B), .in_5(common_1_out_13), .in_6(common_1_instout),
    .in_7(common_1_instadrout), .PSW(PSW), .A(A), .ALU(ALU), .CMEMBUS(pull_resistor_4_node),
    .CFFBUS(pull_resistor_7_node), .CREGBUS(pull_resistor_6_node), .CPSW(pull_resistor_1_node),
    .rdMEM(out_9), .wrMEM(out_8));
  INTR intr_1 (
    .in_1(in_1), .in_2(in_2), .in_3(in_3), .in_4(common_1_out_13), .in_5(common_1_instout), .PSW(PSW),
    .intr(intr3__0), .ADDIVTP(INTRADDR), .CMEMBUS(pull_resistor_4_node), .CFFBUS(pull_resistor_7_node),
    .CREGBUS(pull_resistor_6_node), .rdMEM(out_9), .wrMEM(out_8), .UEXT1__0(UEXT1__0), .inta(inta));

  // Other names for the same wires on the sheet: CLK = in_2; DIN7__0[7:0] = in_4; FCBUS = in_3; MAR[15:0] = ABUS;
  //   MDR[7:0] = DOUTBUS; RD = out_9; rst = in_1; WR = out_8
endmodule

module COMMON (
  input  CLK,
  input  RST,
  input  [7:0] DIN,
  input  [7:0] A,
  input  [7:0] ALU,
  input  [15:0] IVTPPDSP,
  input  [23:0] CMEMBUS,
  input  [9:0] CFFBUS,
  input  [23:0] CREGBUS,
  input  [5:0] CPSW,
  output [15:0] MAR,
  output [7:0] MDR,
  output [3:0] out_13,
  output [10:0] INSTOUT,
  output [3:0] INSTADROUT,
  output [7:0] PSW,
  output [7:0] B
);

  wire ADRINST, adrinst_t, and_1_out, and_2_out, and_3_out, and_4_out, and_5_out, and_6_out, and_7_out,
       and_8_out, and_9_out, and_10_out, and_11_out, and_12_out, and_13_out, and_14_out, and_15_out,
       and_16_out, and_17_out, and_18_out, and_19_out, and_20_out, and_22_out, bezadrinst, branchinst,
       jmpinst, mp2_16b_1_p3, mp4_8b_1_p5, mp4_16b_1_p5, mp8_8b_1_p8, mp8_16b_1_p8, not_1_out, not_5_out,
       or_2_out, or_3_out, or_4_out, or_5_out, or_6_out, or_7_out, or_8_out, reg16_inc_ld_2_p4, rsff_2_p4,
       rsff_3_p4, rsff_4_p4, rsff_6_p4, rsff_7_p4, rsff_8_p3, rsff_8_p4, rsff_9_p3, rsff_9_p4;
  wire [3:0] IR19__16;
  wire [7:0] DWH, DWL, IR7__0, IR15__8;
  wire [7:4] IR23__16;
  wire [15:0] ADDIREG15__0, ADDPCREL15__0, GPR15__0, PC15__0, SP15__0;

  // REG8_LD reg8_ld_1: pin names not known; wires that end beside it: CLK, MDR, {IR23__16, IR19__16}, CREGBUS[6]
  // DC4_16 dc4_16_1: pin names not known; wires that end beside it: IR23__16, PSW[0], bezadrinst, branchinst, jmpinst, adrinst_t
  // DC4_16 dc4_16_2: pin names not known; wires that end beside it: IR19__16, branchinst, INSTOUT[5], INSTOUT[6]
  // MP4_8b mp4_8b_1: pin names not known; wires that end beside it: CREGBUS[2], CREGBUS[1], MDR, IR15__8, mp4_8b_1_p5, GPR15__0[7:0], 1'b1
  // REG8_LD reg8_ld_2: pin names not known; wires that end beside it: CLK, mp4_8b_1_p5, B, CREGBUS[0]
  // ADD16 add16_1: pin names not known; wires that end beside it: {{12{IR15__8[7]}}, IR15__8[6:3]}, ADDIREG15__0, GPR15__0
  // MP8_16b mp8_16b_1: pin names not known; wires that end beside it: CMEMBUS[14], CMEMBUS[6], CMEMBUS[5], PC15__0, {IR7__0, IR15__8}, ADDIREG15__0, SP15__0, mp8_16b_1_p8, IVTPPDSP, 1'b1
  // REG16_INC_LD reg16_inc_ld_1: pin names not known; wires that end beside it: CLK, mp8_16b_1_p8, MAR, CMEMBUS[0], CMEMBUS[1]
  // REG8_LD reg8_ld_3: pin names not known; wires that end beside it: CLK, MDR, IR15__8, CREGBUS[5]
  // DC4_16 dc4_16_3: pin names not known; wires that end beside it: IR19__16, bezadrinst, INSTOUT[0], INSTOUT[1], INSTOUT[2]
  // DC4_16 dc4_16_4: pin names not known; wires that end beside it: IR19__16, jmpinst, INSTOUT[3], INSTOUT[4]
  // REG8_LD reg8_ld_4: pin names not known; wires that end beside it: CLK, MDR, DWH, CREGBUS[8]
  // ADD16 add16_2: pin names not known; wires that end beside it: {{9{IR15__8[7]}}, IR15__8[6:0]}, ADDPCREL15__0, PC15__0
  // MP8_8b mp8_8b_1: pin names not known; wires that end beside it: CMEMBUS[9], CMEMBUS[8], CMEMBUS[7], DIN, A, PC15__0[15:8], PC15__0[7:0], mp8_8b_1_p8, PSW, 1'b1
  // REG8_LD reg8_ld_5: pin names not known; wires that end beside it: CLK, mp8_8b_1_p8, MDR, CMEMBUS[2]
  // REG8_LD reg8_ld_6: pin names not known; wires that end beside it: CLK, MDR, IR7__0, CREGBUS[4]
  // REG8_LD reg8_ld_7: pin names not known; wires that end beside it: CLK, MDR, DWL, CREGBUS[7]
  // MP4_16b mp4_16b_1: pin names not known; wires that end beside it: CMEMBUS[12], CMEMBUS[13], {IR7__0, IR15__8}, ADDPCREL15__0, mp4_16b_1_p5, {DWH, DWL}, 1'b1
  // DC2_4 dc2_4_1: pin names not known; wires that end beside it: IR19__16[3:2], adrinst_t, INSTOUT[7], INSTOUT[8], INSTOUT[9], INSTOUT[10]
  // DC2_4 dc2_4_2: pin names not known; wires that end beside it: IR19__16[1:0], adrinst_t, INSTADROUT[0], INSTADROUT[1], INSTADROUT[2], INSTADROUT[3]
  // REG16 reg16_1: pin names not known; wires that end beside it: CLK, 16'hf000, SP15__0, RST, CMEMBUS[10], CMEMBUS[11]
  not not_1 (not_1_out, RST);
  // RSFF rsff_1: pin names not known; wires that end beside it: CFFBUS[1], CLK, CFFBUS[0], not_1_out, out_13[0]
  // MP2_16b mp2_16b_1: pin names not known; wires that end beside it: RST, mp4_16b_1_p5, mp2_16b_1_p3, 16'h1000, 1'b1
  // REG16_INC_LD reg16_inc_ld_2: pin names not known; wires that end beside it: CLK, mp2_16b_1_p3, PC15__0, reg16_inc_ld_2_p4, CMEMBUS[4]
  or or_1 (reg16_inc_ld_2_p4, CMEMBUS[3], RST);
  // RSFF rsff_2: pin names not known; wires that end beside it: CFFBUS[3], CLK, CFFBUS[2], rsff_2_p4, out_13[1]
  not not_2 (rsff_2_p4, RST);
  and and_1 (and_1_out, ~ALU[7], B[7], A[7]);  // AND_Gate
  or or_2 (or_2_out, and_1_out, and_2_out);
  and and_2 (and_2_out, ALU[7], ~B[7], ~A[7]);  // AND_Gate
  and and_3 (and_3_out, ~ALU[7], ~B[7], A[7]);  // AND_Gate
  or or_3 (or_3_out, and_3_out, and_4_out);
  and and_4 (and_4_out, ALU[7], B[7], ~A[7]);  // AND_Gate
  // RSFF rsff_3: pin names not known; wires that end beside it: CFFBUS[5], CLK, CFFBUS[4], rsff_3_p4, out_13[2]
  not not_3 (rsff_3_p4, RST);
  and and_5 (and_5_out, MDR[1], INSTOUT[2]);
  and and_6 (and_6_out, ADRINST, and_7_out);
  and and_7 (and_7_out, ~A[0], ~A[1], ~A[2], ~A[3], ~A[4], ~A[5], ~A[6], ~A[7]);  // AND_Gate
  and and_8 (and_8_out, MDR[2], INSTOUT[2]);
  and and_9 (and_9_out, ADRINST, A[7]);
  and and_10 (and_10_out, MDR[3], INSTOUT[2]);
  and and_11 (and_11_out, INSTOUT[9], or_2_out);
  or or_4 (or_4_out, and_11_out, and_12_out);
  and and_12 (and_12_out, INSTOUT[10], or_3_out);
  or or_5 (or_5_out, and_5_out, and_6_out);
  or or_6 (or_6_out, and_8_out, and_9_out);
  or or_7 (or_7_out, and_10_out, or_4_out);
  and and_13 (and_13_out, MDR[7], INSTOUT[2]);
  // GPR8x16 gpr8x16_1: pin names not known; wires that end beside it: IR15__8[2:0], CLK, {{9{A[7]}}, A[6:0]}, GPR15__0, CREGBUS[3]
  and and_14 (and_14_out, ~MDR[0], INSTOUT[2], CPSW[5]);  // AND_Gate
  or or_8 (or_8_out, and_14_out, CPSW[0]);
  and and_15 (and_15_out, MDR[0], INSTOUT[2], CPSW[5]);
  and and_16 (and_16_out, ~or_5_out, CPSW[4]);  // AND_Gate
  and and_17 (and_17_out, or_5_out, CPSW[4]);
  and and_18 (and_18_out, ~or_6_out, CPSW[3]);  // AND_Gate
  and and_19 (and_19_out, or_6_out, CPSW[3]);
  // RSFF rsff_4: pin names not known; wires that end beside it: CFFBUS[7], CLK, CFFBUS[6], rsff_4_p4, out_13[3]
  not not_4 (rsff_4_p4, RST);
  or or_9 (ADRINST, INSTOUT[7], INSTOUT[9], INSTOUT[10]);
  not not_5 (not_5_out, RST);
  // RSFF rsff_5: pin names not known; wires that end beside it: or_8_out, CLK, and_15_out, not_5_out, PSW[0]
  // RSFF rsff_6: pin names not known; wires that end beside it: and_16_out, CLK, and_17_out, rsff_6_p4, PSW[1]
  not not_6 (rsff_6_p4, RST);
  // RSFF rsff_7: pin names not known; wires that end beside it: and_18_out, CLK, and_19_out, rsff_7_p4, PSW[2]
  not not_7 (rsff_7_p4, RST);
  and and_20 (and_20_out, ~or_7_out, CPSW[2]);  // AND_Gate
  // RSFF rsff_8: pin names not known; wires that end beside it: and_20_out, CLK, rsff_8_p3, rsff_8_p4, PSW[3]
  and and_21 (rsff_8_p3, or_7_out, CPSW[2]);
  not not_8 (rsff_8_p4, RST);
  and and_22 (and_22_out, ~and_13_out, CPSW[1]);  // AND_Gate
  // RSFF rsff_9: pin names not known; wires that end beside it: and_22_out, CLK, rsff_9_p3, rsff_9_p4, PSW[7]
  and and_23 (rsff_9_p3, and_13_out, CPSW[1]);
  not not_9 (rsff_9_p4, RST);

  // Other names for the same wires on the sheet: A7__0[7:0] = A; ALU7__0[7:0] = ALU; B7__0[7:0] = B;
  //   stFETCH = CFFBUS[0]; clFETCH = CFFBUS[1]; stADDR = CFFBUS[2]; clADDR = CFFBUS[3]; stEXEC = CFFBUS[4];
  //   clEXEC = CFFBUS[5]; stINTR = CFFBUS[6]; clINTR = CFFBUS[7]; ldMAR = CMEMBUS[0]; incMAR = CMEMBUS[1];
  //   ldMDR = CMEMBUS[2]; ldPC = CMEMBUS[3]; incPC = CMEMBUS[4]; mxMAR0 = CMEMBUS[5]; mxMAR1 = CMEMBUS[6];
  //   mxMDR0 = CMEMBUS[7]; mxMDR1 = CMEMBUS[8]; mxMDR2 = CMEMBUS[9]; incSP = CMEMBUS[10]; decSP = CMEMBUS[11];
  //   mxPC1 = CMEMBUS[12]; mxPC0 = CMEMBUS[13]; mxMAR2 = CMEMBUS[14]; clPSWSTART = CPSW[0]; ldI = CPSW[1];
  //   ldV = CPSW[2]; ldN = CPSW[3]; ldZ = CPSW[4]; ldSTART = CPSW[5]; ldB = CREGBUS[0]; mxB0 = CREGBUS[1];
  //   mxB1 = CREGBUS[2]; wrGPR = CREGBUS[3]; ldIR7__0 = CREGBUS[4]; ldIR15__8 = CREGBUS[5]; ldIR23__16 = CREGBUS[6];
  //   ldDWL = CREGBUS[7]; ldDWH = CREGBUS[8]; Din7__0[7:0] = DIN; ENTRADDR15__0[15:0] = IVTPPDSP;
  //   immed = INSTADROUT[0]; memdir = INSTADROUT[1]; regdir = INSTADROUT[2]; regindpom = INSTADROUT[3];
  //   HALT = INSTOUT[0]; RTS = INSTOUT[1]; RTI = INSTOUT[2]; JMP = INSTOUT[3]; JSR = INSTOUT[4]; BLSS = INSTOUT[5];
  //   JLEQ = INSTOUT[6]; LD = INSTOUT[7]; ST = INSTOUT[8]; ADD = INSTOUT[9]; SUB = INSTOUT[10];
  //   IR23__16[3:0] = IR19__16; MAR15__0[15:0] = MAR; MDR7__0[7:0] = MDR; FETCH = out_13[0]; ADDR = out_13[1];
  //   EXEC = out_13[2]; INTR = out_13[3]; PSW7__0[7:0] = PSW; PSWSTART = PSW[0]; PSWZ = PSW[1]; PSWN = PSW[2];
  //   PSWV = PSW[3]; PSWI = PSW[7]

  // Notes on the sheet:
  //   Sabirac
  //   Instrukcijski registar
  //   Pomocni registri
  //   MAR
  //   Dekoderi za prepoznavanje instrukcije na osnovu sadrzaja registra IR23..16
  //   MDR
  //   PC
  //   SP
  //   Dekoderi za prepoznavanje nacina adresiranja
  //   FF za pokretanje FETCH, ADDR, EXEC i INTR faze izvršavanja instrukcije
  //   Registarski fajl
  //   Programska statusna reč (PSW)
endmodule

module FETCH (
  input  in_1,
  input  in_2,
  input  in_3,
  input  [3:0] in_4,
  input  [10:0] in_5,
  input  [3:0] in_6,
  input  [7:0] PSW,
  output [23:0] CMEMBUS,
  output [9:0] CFFBUS,
  output [23:0] CREGBUS,
  output out_11
);

  wire addr2, addr3, addr_t, and_3_out, and_4_out, and_5_out, and_6_out, and_7_out, and_8_out, bezadr1,
       bradr2, brbezadr1, brcnd, brjmp2, brjmp3, brnotfcmem, bruncnd, clFETCH, incPC, jmp3, ldIR7__0,
       ldIR15__8, ldIR23__16, ldMAR, ldMDR, not_1_out, not_3_out, not_4_out, not_5_out, notPSWSTandFETCH,
       or_4_out, or_6_out, rdMEM, reg4_inc_ld_1_p4, reg4_inc_ld_1_p5, reg4_inc_ld_1_p6, stADDR, stEXEC;
  wire [3:0] reg4_inc_ld_1_p3, rom16x24_1_p3;
  wire [23:10] rom16x24_1_p3_2;

  or or_1 (bezadr1, in_5[1], in_5[0], in_5[2]);
  or or_2 (jmp3, in_5[6], in_5[3], in_5[4]);
  not not_1 (not_1_out, in_1);
  // REG4_INC_LD reg4_inc_ld_1: pin names not known; wires that end beside it: in_2, not_1_out, reg4_inc_ld_1_p3, reg4_inc_ld_1_p4, reg4_inc_ld_1_p5, reg4_inc_ld_1_p6
  not not_2 (reg4_inc_ld_1_p6, reg4_inc_ld_1_p5);
  // ROM16x24 rom16x24_1: pin names not known; wires that end beside it: reg4_inc_ld_1_p4, 1'b1, {rom16x24_1_p3_2[23:20], reg4_inc_ld_1_p3, rom16x24_1_p3, rom16x24_1_p3_2[11:10], stEXEC, stADDR, clFETCH, ldIR7__0, ldIR15__8, ldIR23__16, ldMDR, rdMEM, incPC, ldMAR}
  // DC4_16 dc4_16_1: pin names not known; wires that end beside it: rom16x24_1_p3, 1'b1, brjmp3, bruncnd, notPSWSTandFETCH, brbezadr1, brjmp2, bradr2, brnotfcmem
  or or_3 (reg4_inc_ld_1_p5, bruncnd, brcnd);
  or or_4 (or_4_out, in_6[0], in_6[2], in_6[3]);
  or or_5 (addr_t, in_5[7], in_5[8], in_5[9], in_5[10]);
  and and_1 (addr3, in_6[1], addr_t);
  and and_2 (addr2, addr_t, or_4_out);
  not not_3 (not_3_out, in_4[0]);
  not not_4 (not_4_out, PSW[0]);
  or or_6 (or_6_out, not_3_out, not_4_out);
  not not_5 (not_5_out, in_3);
  and and_3 (and_3_out, or_6_out, notPSWSTandFETCH);
  and and_4 (and_4_out, brbezadr1, bezadr1);
  and and_5 (and_5_out, brjmp2, in_5[5]);
  and and_6 (and_6_out, bradr2, addr2);
  and and_7 (and_7_out, brjmp3, jmp3);
  and and_8 (and_8_out, brnotfcmem, not_5_out);
  or or_7 (brcnd, and_3_out, and_4_out, and_5_out, and_6_out, and_7_out, and_8_out);
  assign CMEMBUS[0] = ldMAR ? 1'b1 : 1'bz;  // Controlled_Buffer controlled_buffer_1
  assign CMEMBUS[2] = ldMDR ? 1'b1 : 1'bz;  // Controlled_Buffer controlled_buffer_2
  assign CMEMBUS[4] = incPC ? 1'b1 : 1'bz;  // Controlled_Buffer controlled_buffer_3
  assign CFFBUS[1] = clFETCH ? 1'b1 : 1'bz;  // Controlled_Buffer controlled_buffer_4
  assign CFFBUS[2] = stADDR ? 1'b1 : 1'bz;  // Controlled_Buffer controlled_buffer_5
  assign CFFBUS[4] = stEXEC ? 1'b1 : 1'bz;  // Controlled_Buffer controlled_buffer_6
  assign CREGBUS[4] = ldIR7__0 ? 1'b1 : 1'bz;  // Controlled_Buffer controlled_buffer_7
  assign CREGBUS[5] = ldIR15__8 ? 1'b1 : 1'bz;  // Controlled_Buffer controlled_buffer_8
  assign CREGBUS[6] = ldIR23__16 ? 1'b1 : 1'bz;  // Controlled_Buffer controlled_buffer_9
  assign out_11 = rdMEM ? 1'b1 : 1'bz;  // Controlled_Buffer controlled_buffer_10

  // Other names for the same wires on the sheet: CLK = in_2; FCBUS = in_3; FETCH = in_4[0]; ADDR = in_4[1];
  //   EXEC = in_4[2]; INTR = in_4[3]; HALT = in_5[0]; RTS = in_5[1]; RTI = in_5[2]; JMP = in_5[3]; JSR = in_5[4];
  //   BLSS = in_5[5]; jmp2 = in_5[5]; JLEQ = in_5[6]; LD = in_5[7]; ST = in_5[8]; ADD = in_5[9]; SUB = in_5[10];
  //   immed = in_6[0]; memdir = in_6[1]; regdir = in_6[2]; regindpom = in_6[3]; PSWSTART = PSW[0]; rst = in_1

  // Notes on the sheet:
  //   Operaciona jedinica
  //   Kontrolna jedinica
endmodule

module ADDR (
  input  in_1,
  input  in_2,
  input  in_3,
  input  [3:0] in_4,
  input  [10:0] in_5,
  input  [3:0] in_6,
  output [23:0] CMEMBUS,
  output [9:0] CFFBUS,
  output [23:0] CREGBUS,
  output out_10
);

  wire and_1_out, and_2_out, and_3_out, bradr, brcnd, brnotADDR, brnotfcbus, brSTORE, bruncnd, clADDR, ldB,
       ldMAR, ldMDR, mp2_4b_1_p3, mxB0, mxB1, mxMAR0, mxMAR1, not_1_out, not_3_out, not_4_out, rdMEM,
       reg4_inc_ld_1_p4, reg4_inc_ld_1_p5, reg4_inc_ld_1_p6, stEXEC;
  wire [3:0] kmadr_1_adr3__0, mp2_4b_1_p2;
  wire [12:10] rom16x17_1_p3;

  not not_1 (not_1_out, in_1);
  KMADR kmadr_1 (.immed(in_6[0]), .memdir(in_6[1]), .regdir(in_6[2]), .regindpom(in_6[3]), .Adr3__0(kmadr_1_adr3__0));
  // MP2_4b mp2_4b_1: pin names not known; wires that end beside it: bradr, mp2_4b_1_p2, mp2_4b_1_p3, kmadr_1_adr3__0
  // REG4_INC_LD reg4_inc_ld_1: pin names not known; wires that end beside it: in_2, not_1_out, mp2_4b_1_p3, reg4_inc_ld_1_p4, reg4_inc_ld_1_p5, reg4_inc_ld_1_p6
  not not_2 (reg4_inc_ld_1_p6, reg4_inc_ld_1_p5);
  // ROM16x17 rom16x17_1: pin names not known; wires that end beside it: reg4_inc_ld_1_p4, 1'b1, {mp2_4b_1_p2, rom16x17_1_p3, stEXEC, clADDR, ldMDR, rdMEM, mxMAR1, mxB1, mxMAR0, ldMAR, mxB0, ldB}
  // DC3_8 dc3_8_1: pin names not known; wires that end beside it: rom16x17_1_p3, 1'b1, bruncnd, brnotADDR, brSTORE, brnotfcbus, bradr
  or or_1 (reg4_inc_ld_1_p5, bruncnd, brcnd, bradr);
  not not_3 (not_3_out, in_4[1]);
  not not_4 (not_4_out, in_3);
  and and_1 (and_1_out, not_3_out, brnotADDR);
  and and_2 (and_2_out, in_5[8], brSTORE);
  and and_3 (and_3_out, brnotfcbus, not_4_out);
  or or_2 (brcnd, and_1_out, and_2_out, and_3_out);
  assign CMEMBUS[0] = ldMAR ? 1'b1 : 1'bz;  // Controlled_Buffer controlled_buffer_1
  assign CMEMBUS[2] = ldMDR ? 1'b1 : 1'bz;  // Controlled_Buffer controlled_buffer_2
  assign CMEMBUS[5] = mxMAR0 ? 1'b1 : 1'bz;  // Controlled_Buffer controlled_buffer_3
  assign CMEMBUS[6] = mxMAR1 ? 1'b1 : 1'bz;  // Controlled_Buffer controlled_buffer_4
  assign CFFBUS[3] = clADDR ? 1'b1 : 1'bz;  // Controlled_Buffer controlled_buffer_5
  assign CFFBUS[4] = stEXEC ? 1'b1 : 1'bz;  // Controlled_Buffer controlled_buffer_6
  assign CREGBUS[0] = ldB ? 1'b1 : 1'bz;  // Controlled_Buffer controlled_buffer_7
  assign CREGBUS[1] = mxB0 ? 1'b1 : 1'bz;  // Controlled_Buffer controlled_buffer_8
  assign CREGBUS[2] = mxB1 ? 1'b1 : 1'bz;  // Controlled_Buffer controlled_buffer_9
  assign out_10 = rdMEM ? 1'b1 : 1'bz;  // Controlled_Buffer controlled_buffer_10

  // Other names for the same wires on the sheet: CLK = in_2; FCBUS = in_3; ADDR = in_4[1]; ST = in_5[8];
  //   immed = in_6[0]; memdir = in_6[1]; regdir = in_6[2]; regindpom = in_6[3]; rst = in_1

  // Notes on the sheet:
  //   Operaciona jedinica
  //   Upravljacka jedinica
endmodule

module EXEC (
  input  in_1,
  input  in_2,
  input  in_3,
  input  [7:0] B,
  input  [3:0] in_5,
  input  [10:0] in_6,
  input  [3:0] in_7,
  input  [7:0] PSW,
  output [7:0] A,
  output [7:0] ALU,
  output [23:0] CMEMBUS,
  output [9:0] CFFBUS,
  output [23:0] CREGBUS,
  output [5:0] CPSW,
  output rdMEM,
  output wrMEM
);

  wire add_t, and_1_out, and_2_out, and_3_out, and_4_out, and_5_out, and_6_out, and_7_out, brcnd, brimmed,
       brnotbrorjmp, brnotEXEC, brnotFCBUS, bropr, brorjmp, brregdir, bruncnd, clEXEC, clPSWSTART, decSP,
       incSP, ldA, ldDWH, ldDWL, ldI, ldMAR, ldMDR, ldN, ldPC, ldSTART, ldV, ldZ, mp2_6b_1_p2, mp2_8b_1_p3,
       mxA0, mxMAR0, mxMAR1, mxMDR0, mxMDR1, mxPC0, mxPC1, not_1_out, not_2_out, not_3_out, not_4_out,
       not_5_out, not_6_out, or_1_out, or_2_out, rdMEM_t, stINTR, sub_t, wrGPR, wrMEM_t, xor_1_out;
  wire [5:0] kmopr_1_adr5__0, mp2_6b_1_p3, reg6_inc_ld_1_a5__0;
  wire [30:28] dc3_8_1_p1;

  // MP2_8b mp2_8b_1: pin names not known; wires that end beside it: mxA0, B, mp2_8b_1_p3, ALU, 1'b1
  not not_1 (not_1_out, in_1);
  // REG8_LD reg8_ld_1: pin names not known; wires that end beside it: in_2, not_1_out, mp2_8b_1_p3, A, ldA
  not not_2 (not_2_out, in_1);
  // DC3_8 dc3_8_1: pin names not known; wires that end beside it: dc3_8_1_p1, 1'b1, bruncnd, brnotEXEC, brimmed, brregdir, brnotbrorjmp, brnotFCBUS, bropr
  KMOPR kmopr_1 (
    .LD(in_6[7]), .ST(in_6[8]), .ADD(in_6[9]), .SUB(in_6[10]), .BLSS(in_6[5]), .JLEQ(in_6[6]), .JMP(in_6[3]),
    .JSR(in_6[4]), .RTS(in_6[1]), .RTI(in_6[2]), .HALT(in_6[0]), .Adr5__0(kmopr_1_adr5__0));
  // MP2_6b mp2_6b_1: pin names not known; wires that end beside it: bropr, mp2_6b_1_p2, mp2_6b_1_p3, kmopr_1_adr5__0, 1'b1
  REG6_INC_LD reg6_inc_ld_1 (
    .I5__0(mp2_6b_1_p3), .LD(or_1_out), .INC(not_3_out), .mr(not_2_out), .CLK(in_2),
    .A5__0(reg6_inc_ld_1_a5__0));
  not not_3 (not_3_out, or_1_out);
  // ROM64x37 rom64x37_1: pin names not known; wires that end beside it: reg6_inc_ld_1_a5__0, 1'b1, mp2_6b_1_p2, {dc3_8_1_p1, clEXEC, stINTR, clPSWSTART, ldSTART, ldI, mxPC1, ldDWH, ldDWL, rdMEM_t, incSP, mxMDR1, decSP, ldMAR, mxMAR1, mxMAR0, ldPC, mxPC0, sub_t, ldV, add_t, mxA0, wrGPR, wrMEM_t, ldMDR, mxMDR0, ldZ, ldN, ldA}
  or or_1 (or_1_out, bruncnd, brcnd, bropr);
  // ALU8_ADD_SUB alu8_add_sub_1: pin names not known; wires that end beside it: A, ALU, B, 1'b0, add_t, sub_t
  not not_4 (not_4_out, in_5[2]);
  not not_5 (not_5_out, brorjmp);
  not not_6 (not_6_out, in_3);
  and and_1 (and_1_out, not_4_out, brnotEXEC);
  and and_2 (and_2_out, in_7[0], brimmed);
  and and_3 (and_3_out, in_7[2], brregdir);
  and and_4 (and_4_out, not_5_out, brnotbrorjmp);
  and and_5 (and_5_out, not_6_out, brnotFCBUS);
  xor xor_1 (xor_1_out, PSW[2], PSW[3]);
  or or_2 (or_2_out, xor_1_out, PSW[1]);
  or or_3 (brcnd, and_1_out, and_2_out, and_3_out, and_4_out, and_5_out);
  and and_6 (and_6_out, xor_1_out, in_6[5]);
  and and_7 (and_7_out, or_2_out, in_6[6]);
  or or_4 (brorjmp, and_6_out, and_7_out);
  assign CMEMBUS[0] = ldMAR ? 1'b1 : 1'bz;  // Controlled_Buffer controlled_buffer_1
  assign CMEMBUS[2] = ldMDR ? 1'b1 : 1'bz;  // Controlled_Buffer controlled_buffer_2
  assign CMEMBUS[3] = ldPC ? 1'b1 : 1'bz;  // Controlled_Buffer controlled_buffer_3
  assign CMEMBUS[5] = mxMAR0 ? 1'b1 : 1'bz;  // Controlled_Buffer controlled_buffer_4
  assign CMEMBUS[6] = mxMAR1 ? 1'b1 : 1'bz;  // Controlled_Buffer controlled_buffer_5
  assign CMEMBUS[7] = mxMDR0 ? 1'b1 : 1'bz;  // Controlled_Buffer controlled_buffer_6
  assign CMEMBUS[8] = mxMDR1 ? 1'b1 : 1'bz;  // Controlled_Buffer controlled_buffer_7
  assign CMEMBUS[10] = incSP ? 1'b1 : 1'bz;  // Controlled_Buffer controlled_buffer_8
  assign CMEMBUS[11] = decSP ? 1'b1 : 1'bz;  // Controlled_Buffer controlled_buffer_9
  assign CMEMBUS[12] = mxPC1 ? 1'b1 : 1'bz;  // Controlled_Buffer controlled_buffer_10
  assign CMEMBUS[13] = mxPC0 ? 1'b1 : 1'bz;  // Controlled_Buffer controlled_buffer_11
  assign CFFBUS[5] = clEXEC ? 1'b1 : 1'bz;  // Controlled_Buffer controlled_buffer_12
  assign CFFBUS[6] = stINTR ? 1'b1 : 1'bz;  // Controlled_Buffer controlled_buffer_13
  assign CREGBUS[3] = wrGPR ? 1'b1 : 1'bz;  // Controlled_Buffer controlled_buffer_14
  assign CREGBUS[7] = ldDWL ? 1'b1 : 1'bz;  // Controlled_Buffer controlled_buffer_15
  assign CREGBUS[8] = ldDWH ? 1'b1 : 1'bz;  // Controlled_Buffer controlled_buffer_16
  assign CPSW[0] = clPSWSTART ? 1'b1 : 1'bz;  // Controlled_Buffer controlled_buffer_17
  assign CPSW[1] = ldI ? 1'b1 : 1'bz;  // Controlled_Buffer controlled_buffer_18
  assign CPSW[2] = ldV ? 1'b1 : 1'bz;  // Controlled_Buffer controlled_buffer_19
  assign CPSW[3] = ldN ? 1'b1 : 1'bz;  // Controlled_Buffer controlled_buffer_20
  assign CPSW[4] = ldZ ? 1'b1 : 1'bz;  // Controlled_Buffer controlled_buffer_21
  assign CPSW[5] = ldSTART ? 1'b1 : 1'bz;  // Controlled_Buffer controlled_buffer_22
  assign rdMEM = rdMEM_t ? 1'b1 : 1'bz;  // Controlled_Buffer controlled_buffer_23
  assign wrMEM = wrMEM_t ? 1'b1 : 1'bz;  // Controlled_Buffer controlled_buffer_24

  // Other names for the same wires on the sheet: A7__0[7:0] = A; ALU7__0[7:0] = ALU; B7__0[7:0] = B; CLK = in_2;
  //   FCBUS = in_3; EXEC = in_5[2]; HALT = in_6[0]; RTS = in_6[1]; RTI = in_6[2]; JMP = in_6[3]; JSR = in_6[4];
  //   BLSS = in_6[5]; JLEQ = in_6[6]; LD = in_6[7]; ST = in_6[8]; ADD = in_6[9]; SUB = in_6[10]; immed = in_7[0];
  //   regdir = in_7[2]; PSWZ = PSW[1]; PSWN = PSW[2]; PSWV = PSW[3]; rst = in_1

  // Notes on the sheet:
  //   Operaciona jedinica
  //   Upravljacka jedinica
  //   Akumulator
  //   ALU
  //   Uslov za skok
endmodule

module INTR (
  input  in_1,
  input  in_2,
  input  in_3,
  input  [3:0] in_4,
  input  [10:0] in_5,
  input  [7:0] PSW,
  input  [3:0] intr,
  output [15:0] ADDIVTP,
  output [1:0] UEXT1__0,
  output inta,
  output [23:0] CMEMBUS,
  output [9:0] CFFBUS,
  output [23:0] CREGBUS,
  output rdMEM,
  output wrMEM
);

  wire and_2_out, and_3_out, and_4_out, brcnd, brnotFCBUS, brnotINTR, brnotprekid, bruncnd, clINTR, decSP,
       incMAR, ldDWH, ldDWL, ldMAR, ldMDR, ldPC, mxMAR0, mxMAR1, mxMAR2, mxMDR0, mxMDR1, mxMDR2, mxPC1,
       not_1_out, not_2_out, not_3_out, not_5_out, not_6_out, not_7_out, prekid, prper, rdMEM_t,
       reg4_inc_ld_1_p4, reg4_inc_ld_1_p5, reg4_inc_ld_1_p6, stFETCH, wrMEM_t;
  wire [2:0] dc3_8_1_p1;
  wire [2:1] IVTDSP15__0;
  wire [3:0] reg4_inc_ld_1_p3;
  wire [15:0] IVTP15__0;

  and and_1 (prekid, prper, 1'b1, not_2_out);
  not not_1 (not_1_out, in_1);
  // REG4_INC_LD reg4_inc_ld_1: pin names not known; wires that end beside it: in_2, not_1_out, reg4_inc_ld_1_p3, reg4_inc_ld_1_p4, reg4_inc_ld_1_p5, reg4_inc_ld_1_p6
  // DC3_8 dc3_8_1: pin names not known; wires that end beside it: dc3_8_1_p1, 1'b1, bruncnd, brnotINTR, brnotprekid, brnotFCBUS
  not not_2 (not_2_out, in_5[0]);
  not not_3 (not_3_out, in_1);
  // REG16_LD reg16_ld_1: pin names not known; wires that end beside it: in_2, not_3_out, IVTP15__0, PSW[7]
  not not_4 (reg4_inc_ld_1_p6, reg4_inc_ld_1_p5);
  // ROM16x26 rom16x26_1: pin names not known; wires that end beside it: reg4_inc_ld_1_p4, 1'b1, {reg4_inc_ld_1_p3, dc3_8_1_p1, clINTR, stFETCH, mxPC1, ldPC, ldDWH, ldDWL, incMAR, rdMEM_t, mxMAR2, inta, mxMDR2, mxMDR0, wrMEM_t, ldMDR, mxMDR1, decSP, ldMAR, mxMAR1, mxMAR0}
  or or_1 (prper, intr[3], intr[2], intr[1], intr[0]);
  or or_2 (reg4_inc_ld_1_p5, bruncnd, brcnd);
  // CD4 cd4_1: pin names not known; wires that end beside it: intr[3], intr[2], intr[1], intr[0], 1'b1, UEXT1__0[1], UEXT1__0[0]
  // REG2_LD reg2_ld_1: pin names not known; wires that end beside it: in_2, UEXT1__0, IVTDSP15__0, inta
  // ADD16 add16_1: pin names not known; wires that end beside it: IVTP15__0, ADDIVTP, {{13{1'b0}}, IVTDSP15__0, 1'b0}, 1'b0
  not not_5 (not_5_out, in_4[3]);
  not not_6 (not_6_out, prekid);
  not not_7 (not_7_out, in_3);
  and and_2 (and_2_out, not_5_out, brnotINTR);
  and and_3 (and_3_out, not_6_out, brnotprekid);
  and and_4 (and_4_out, not_7_out, brnotFCBUS);
  or or_3 (brcnd, and_2_out, and_3_out, and_4_out);
  assign CMEMBUS[0] = ldMAR ? 1'b1 : 1'bz;  // Controlled_Buffer controlled_buffer_1
  assign CMEMBUS[1] = incMAR ? 1'b1 : 1'bz;  // Controlled_Buffer controlled_buffer_2
  assign CMEMBUS[2] = ldMDR ? 1'b1 : 1'bz;  // Controlled_Buffer controlled_buffer_3
  assign CMEMBUS[3] = ldPC ? 1'b1 : 1'bz;  // Controlled_Buffer controlled_buffer_4
  assign CMEMBUS[5] = mxMAR0 ? 1'b1 : 1'bz;  // Controlled_Buffer controlled_buffer_5
  assign CMEMBUS[6] = mxMAR1 ? 1'b1 : 1'bz;  // Controlled_Buffer controlled_buffer_6
  assign CMEMBUS[7] = mxMDR0 ? 1'b1 : 1'bz;  // Controlled_Buffer controlled_buffer_7
  assign CMEMBUS[8] = mxMDR1 ? 1'b1 : 1'bz;  // Controlled_Buffer controlled_buffer_8
  assign CMEMBUS[9] = mxMDR2 ? 1'b1 : 1'bz;  // Controlled_Buffer controlled_buffer_9
  assign CMEMBUS[11] = decSP ? 1'b1 : 1'bz;  // Controlled_Buffer controlled_buffer_10
  assign CMEMBUS[12] = mxPC1 ? 1'b1 : 1'bz;  // Controlled_Buffer controlled_buffer_11
  assign CMEMBUS[14] = mxMAR2 ? 1'b1 : 1'bz;  // Controlled_Buffer controlled_buffer_12
  assign CFFBUS[0] = stFETCH ? 1'b1 : 1'bz;  // Controlled_Buffer controlled_buffer_13
  assign CFFBUS[7] = clINTR ? 1'b1 : 1'bz;  // Controlled_Buffer controlled_buffer_14
  assign CREGBUS[0] = inta ? 1'b1 : 1'bz;  // Controlled_Buffer controlled_buffer_15
  assign CREGBUS[7] = ldDWL ? 1'b1 : 1'bz;  // Controlled_Buffer controlled_buffer_16
  assign CREGBUS[8] = ldDWH ? 1'b1 : 1'bz;  // Controlled_Buffer controlled_buffer_17
  assign rdMEM = rdMEM_t ? 1'b1 : 1'bz;  // Controlled_Buffer controlled_buffer_18
  assign wrMEM = wrMEM_t ? 1'b1 : 1'bz;  // Controlled_Buffer controlled_buffer_19

  // Other names for the same wires on the sheet: ldBR = inta; ADDIVTP15__0[15:0] = ADDIVTP; CLK = in_2; FCBUS = in_3;
  //   INTR_t = in_4[3]; HALT = in_5[0]; intr3__0[3:0] = intr; PSWI = PSW[7]; rst = in_1

  // Notes on the sheet:
  //   Operaciona jedinica
  //   Upravljacka jedinica
endmodule

module RAM (
  input  [15:0] in_1,
  input  in_2,
  input  [7:0] in_3,
  input  in_4,
  input  in_5,
  input  in_6,
  output [7:0] out_7,
  output out_8
);

  wire and_1_out, and_2_out, CNT0, LDCNT, not_1_out, notCNT0, or_1_out, reg4_ld_sl_sr_1_p6, rsff_2_p4,
       rsff_2_p5, rsff_3_p4, sl;
  wire [3:0] CNT, LFSR;

  // RSFF rsff_1: pin names not known; wires that end beside it: 1'b0, in_2, in_6, sl
  or or_1 (or_1_out, in_4, in_5);
  // REG4_LD_SL_SR reg4_ld_sl_sr_1: pin names not known; wires that end beside it: 1'b0, 1'b0, in_2, 4'b1111, LFSR, reg4_ld_sl_sr_1_p6, sl, in_6
  // RisingEdge risingedge_1: pin names not known; wires that end beside it: or_1_out, in_2, LDCNT
  // MEM64Kx8 mem64kx8_1: pin names not known; wires that end beside it: in_1, 1'b1, in_2, in_3, out_7, in_4
  xor xor_1 (reg4_ld_sl_sr_1_p6, LFSR[2], LFSR[3]);
  and and_1 (and_1_out, CNT0, not_1_out);
  not not_1 (not_1_out, LDCNT);
  // RSFF rsff_2: pin names not known; wires that end beside it: and_1_out, in_2, LDCNT, rsff_2_p4, rsff_2_p5
  not not_2 (rsff_2_p4, in_6);
  and and_2 (and_2_out, rsff_2_p5, CNT0);
  // REG4m_DEC_LD reg4m_dec_ld_1: pin names not known; wires that end beside it: in_2, LFSR, CNT, LDCNT, notCNT0, notCNT0
  or or_2 (notCNT0, CNT[0], CNT[1], CNT[2], CNT[3]);
  // RSFF rsff_3: pin names not known; wires that end beside it: out_8, in_2, and_2_out, rsff_3_p4, out_8
  not not_3 (rsff_3_p4, in_6);
  not not_4 (CNT0, notCNT0);

  // Other names for the same wires on the sheet: ADR[15:0] = in_1; CLK = in_2; DIN[7:0] = in_3; DOUT[7:0] = out_7;
  //   fc = out_8; RDMEM = in_5; rst = in_6; WRMEM = in_4

  // Notes on the sheet:
  //   Random broj predstavlja vreme pristupa memoriji
  //   Brojac za generisanje random broja 
  //   Jedinica za generisanje function complete (fc) signala
  //   Brojac za dekrementiranje random broja
endmodule
