// Logisim project ORT2Project_nijemoj.circ as structural Verilog
module COMPUTER (
);

  wire button_1_out, CLK, pull_resistor_4_node, pull_resistor_6_node, ram_1_out_8, rst;
  wire [7:0] pull_resistor_1_node, ram_1_out_7;
  wire [15:0] pull_resistor_3_node;

  Button button_1 (.out(button_1_out));
  Clock u_CLK (.out(CLK));
  // RisingEdge risingedge_1: pin names not known; wires that end beside it: button_1_out, CLK, rst
  RAM ram_1 (
    .in_1(pull_resistor_3_node), .in_2(CLK), .in_3(pull_resistor_1_node), .in_4(pull_resistor_4_node),
    .in_5(pull_resistor_6_node), .in_6(rst), .out_7(ram_1_out_7), .out_8(ram_1_out_8));
  Pull_Resistor pull_resistor_1 (.node(pull_resistor_1_node));
  Pull_Resistor pull_resistor_2 (.node(ram_1_out_7));
  Pull_Resistor pull_resistor_3 (.node(pull_resistor_3_node));
  Pull_Resistor pull_resistor_4 (.node(pull_resistor_4_node));
  Pull_Resistor pull_resistor_5 (.node(ram_1_out_8));
  Pull_Resistor pull_resistor_6 (.node(pull_resistor_6_node));
  CPU cpu_1 (
    .in_1(rst), .in_2(CLK), .in_3(ram_1_out_8), .in_4(ram_1_out_7), .ABUS(pull_resistor_3_node),
    .DOUTBUS(pull_resistor_1_node), .out_7(pull_resistor_4_node), .out_8(pull_resistor_6_node));
endmodule

module CPU (
  input  in_1,
  input  in_2,
  input  in_3,
  input  [7:0] in_4,
  output [15:0] ABUS,
  output [7:0] DOUTBUS,
  output out_7,
  output out_8
);

  wire [3:0] common_1_instadrout, common_1_out_9;
  wire [7:0] PSW;
  wire [9:0] pull_resistor_4_node;
  wire [10:0] common_1_instout;
  wire [23:0] pull_resistor_3_node, pull_resistor_6_node;

  COMMON common_1 (
    .CLK(in_2), .RST(in_1), .DIN(in_4), .CMEMBUS(pull_resistor_6_node), .MAR(ABUS), .MDR(DOUTBUS),
    .out_9(common_1_out_9), .INSTOUT(common_1_instout), .INSTADROUT(common_1_instadrout), .PSW(PSW),
    .CREGBUS(pull_resistor_3_node), .CFFBUS(pull_resistor_4_node));
  Pull_Resistor pull_resistor_1 (.node(common_1_instout));
  Pull_Resistor pull_resistor_2 (.node(common_1_out_9));
  Pull_Resistor pull_resistor_3 (.node(pull_resistor_3_node));
  Pull_Resistor pull_resistor_4 (.node(pull_resistor_4_node));
  Pull_Resistor pull_resistor_5 (.node(common_1_instadrout));
  Pull_Resistor pull_resistor_6 (.node(pull_resistor_6_node));
  FETCH fetch_1 (
    .in_1(in_1), .in_2(in_2), .in_3(in_3), .in_4(common_1_out_9), .in_5(common_1_instout),
    .in_6(common_1_instadrout), .PSW(PSW), .out_11(out_8), .CMEMBUS(pull_resistor_6_node),
    .CFFBUS(pull_resistor_4_node), .CREGBUS(pull_resistor_3_node));

  // Other names for the same wires on the sheet: CLK = in_2; DIN7__0[7:0] = in_4; FCBUS = in_3; MAR[15:0] = ABUS;
  //   MDR[7:0] = DOUTBUS; RD = out_8; rst = in_1; WR = out_7
endmodule

module COMMON (
  input  CLK,
  input  RST,
  input  [7:0] DIN,
  input  [23:0] CMEMBUS,
  input  [9:0] CFFBUS,
  input  [23:0] CREGBUS,
  output [15:0] MAR,
  output [7:0] MDR,
  output [3:0] out_9,
  output [10:0] INSTOUT,
  output [3:0] INSTADROUT,
  output [7:0] PSW
);

  wire adrinst, bezadrinst, branchinst, jmpinst, mp2_16b_1_p3, not_1_out, not_4_out, reg16_inc_ld_2_p4,
       rsff_2_p4, rsff_3_p4, rsff_5_p4, stPSWSTART;
  wire [3:0] IR19__16;
  wire [7:0] IR7__0, IR15__8;
  wire [7:4] IR23__16;
  wire [15:0] inPC, PC15__0;

  // REG8_LD reg8_ld_1: pin names not known; wires that end beside it: CLK, MDR, {IR23__16, IR19__16}, CREGBUS[6]
  // REG16_INC_LD reg16_inc_ld_1: pin names not known; wires that end beside it: CLK, PC15__0, MAR, CMEMBUS[0], CMEMBUS[1]
  // DC4_16 dc4_16_1: pin names not known; wires that end beside it: IR23__16, PSW[0], bezadrinst, branchinst, jmpinst, adrinst
  // DC4_16 dc4_16_2: pin names not known; wires that end beside it: IR19__16, branchinst, INSTOUT[5], INSTOUT[6]
  // REG8_LD reg8_ld_2: pin names not known; wires that end beside it: CLK, MDR, IR15__8, CREGBUS[5]
  // REG8_LD reg8_ld_3: pin names not known; wires that end beside it: CLK, DIN, MDR, CMEMBUS[2]
  // DC4_16 dc4_16_3: pin names not known; wires that end beside it: IR19__16, bezadrinst, INSTOUT[0], INSTOUT[1], INSTOUT[2]
  // DC4_16 dc4_16_4: pin names not known; wires that end beside it: IR19__16, jmpinst, INSTOUT[3], INSTOUT[4]
  // REG8_LD reg8_ld_4: pin names not known; wires that end beside it: CLK, MDR, IR7__0, CREGBUS[4]
  // DC2_4 dc2_4_1: pin names not known; wires that end beside it: IR19__16[3:2], adrinst, INSTOUT[7], INSTOUT[8], INSTOUT[9], INSTOUT[10]
  // DC2_4 dc2_4_2: pin names not known; wires that end beside it: IR19__16[1:0], adrinst, INSTADROUT[0], INSTADROUT[1], INSTADROUT[2], INSTADROUT[3]
  not not_1 (not_1_out, RST);
  // RSFF rsff_1: pin names not known; wires that end beside it: CFFBUS[1], CLK, CFFBUS[0], not_1_out, out_9[0]
  // MP2_16b mp2_16b_1: pin names not known; wires that end beside it: RST, inPC, mp2_16b_1_p3, 16'h1000, 1'b1
  // REG16_INC_LD reg16_inc_ld_2: pin names not known; wires that end beside it: CLK, mp2_16b_1_p3, PC15__0, reg16_inc_ld_2_p4, CMEMBUS[4]
  or or_1 (reg16_inc_ld_2_p4, CMEMBUS[3], RST);
  // RSFF rsff_2: pin names not known; wires that end beside it: CFFBUS[3], CLK, CFFBUS[2], rsff_2_p4, out_9[1]
  not not_2 (rsff_2_p4, RST);
  // RSFF rsff_3: pin names not known; wires that end beside it: CFFBUS[5], CLK, CFFBUS[4], rsff_3_p4, out_9[2]
  not not_3 (rsff_3_p4, RST);
  not not_4 (not_4_out, RST);
  // RSFF rsff_4: pin names not known; wires that end beside it: CFFBUS[8], CLK, stPSWSTART, not_4_out, PSW[0]
  // RSFF rsff_5: pin names not known; wires that end beside it: CFFBUS[7], CLK, CFFBUS[6], rsff_5_p4, out_9[3]
  not not_5 (rsff_5_p4, RST);

  // Other names for the same wires on the sheet: stFETCH = CFFBUS[0]; clFETCH = CFFBUS[1]; stADDR = CFFBUS[2];
  //   clADDR = CFFBUS[3]; stEXEC = CFFBUS[4]; clEXEC = CFFBUS[5]; stINTR = CFFBUS[6]; clINTR = CFFBUS[7];
  //   clPSWSTART = CFFBUS[8]; ldMAR = CMEMBUS[0]; incMAR = CMEMBUS[1]; ldMDR = CMEMBUS[2]; ldPC = CMEMBUS[3];
  //   incPC = CMEMBUS[4]; ldIR7__0 = CREGBUS[4]; ldIR15__8 = CREGBUS[5]; ldIR23__16 = CREGBUS[6]; Din7__0[7:0] = DIN;
  //   immed = INSTADROUT[0]; memdir = INSTADROUT[1]; regdir = INSTADROUT[2]; regindpom = INSTADROUT[3];
  //   HALT = INSTOUT[0]; RTS = INSTOUT[1]; RTI = INSTOUT[2]; JMP = INSTOUT[3]; JSR = INSTOUT[4]; BLSS = INSTOUT[5];
  //   JLEQ = INSTOUT[6]; LD = INSTOUT[7]; ST = INSTOUT[8]; ADD = INSTOUT[9]; SUB = INSTOUT[10];
  //   IR23__16[3:0] = IR19__16; MAR15__0[15:0] = MAR; MDR7__0[7:0] = MDR; FETCH = out_9[0]; ADDR = out_9[1];
  //   EXEC = out_9[2]; INTR = out_9[3]; PSWSTART = PSW[0]

  // Notes on the sheet:
  //   Instrukcijski registar
  //   MAR
  //   Dekoderi za prepoznavanje instrukcije na osnovu sadrzaja registra IR23..16
  //   MDR
  //   PC
  //   Dekoderi za prepoznavanje nacina adresiranja
  //   FF za pokretanje FETCH, ADDR, EXEC i INTR faze izvršavanja instrukcije
  //   Programska statusna reč (PSW)
endmodule

module FETCH (
  input  in_1,
  input  in_2,
  input  in_3,
  input  [3:0] in_4,
  input  [10:0] in_5,
  input  [3:0] in_6,
  input  [7:0] PSW,
  output [23:0] CMEMBUS,
  output [9:0] CFFBUS,
  output [23:0] CREGBUS,
  output out_11
);

  wire addr2, addr3, addr_t, and_3_out, and_4_out, and_5_out, and_6_out, and_7_out, and_8_out, bezadr1,
       bradr2, brbezadr1, brcnd, brjmp2, brjmp3, brnotfcmem, bruncnd, clFETCH, incPC, jmp3, ldIR7__0,
       ldIR15__8, ldIR23__16, ldMAR, ldMDR, not_1_out, not_3_out, not_4_out, not_5_out, notPSWSTandFETCH,
       or_4_out, or_6_out, rdMEM, reg4_inc_ld_1_p4, reg4_inc_ld_1_p5, reg4_inc_ld_1_p6, stADDR, stEXEC;
  wire [3:0] reg4_inc_ld_1_p3, rom16x24_1_p3;
  wire [23:10] rom16x24_1_p3_2;

  or or_1 (bezadr1, in_5[1], in_5[0], in_5[2]);
  or or_2 (jmp3, in_5[6], in_5[3], in_5[4]);
  not not_1 (not_1_out, in_1);
  // REG4_INC_LD reg4_inc_ld_1: pin names not known; wires that end beside it: in_2, not_1_out, reg4_inc_ld_1_p3, reg4_inc_ld_1_p4, reg4_inc_ld_1_p5, reg4_inc_ld_1_p6
  not not_2 (reg4_inc_ld_1_p6, reg4_inc_ld_1_p5);
  // ROM16x24 rom16x24_1: pin names not known; wires that end beside it: reg4_inc_ld_1_p4, 1'b1, {rom16x24_1_p3_2[23:20], reg4_inc_ld_1_p3, rom16x24_1_p3, rom16x24_1_p3_2[11:10], stEXEC, stADDR, clFETCH, ldIR7__0, ldIR15__8, ldIR23__16, ldMDR, rdMEM, incPC, ldMAR}
  // DC4_16 dc4_16_1: pin names not known; wires that end beside it: rom16x24_1_p3, 1'b1, brjmp3, bruncnd, notPSWSTandFETCH, brbezadr1, brjmp2, bradr2, brnotfcmem
  or or_3 (reg4_inc_ld_1_p5, bruncnd, brcnd);
  or or_4 (or_4_out, in_6[0], in_6[2], in_6[3]);
  or or_5 (addr_t, in_5[7], in_5[8], in_5[9], in_5[10]);
  and and_1 (addr3, in_6[1], addr_t);
  and and_2 (addr2, addr_t, or_4_out);
  not not_3 (not_3_out, in_4[0]);
  not not_4 (not_4_out, PSW[0]);
  or or_6 (or_6_out, not_3_out, not_4_out);
  not not_5 (not_5_out, in_3);
  and and_3 (and_3_out, or_6_out, notPSWSTandFETCH);
  and and_4 (and_4_out, brbezadr1, bezadr1);
  and and_5 (and_5_out, brjmp2, in_5[5]);
  and and_6 (and_6_out, bradr2, addr2);
  and and_7 (and_7_out, brjmp3, jmp3);
  and and_8 (and_8_out, brnotfcmem, not_5_out);
  or or_7 (brcnd, and_3_out, and_4_out, and_5_out, and_6_out, and_7_out, and_8_out);
  assign CMEMBUS[0] = ldMAR ? 1'b1 : 1'bz;  // Controlled_Buffer controlled_buffer_1
  assign CMEMBUS[2] = ldMDR ? 1'b1 : 1'bz;  // Controlled_Buffer controlled_buffer_2
  assign CMEMBUS[4] = incPC ? 1'b1 : 1'bz;  // Controlled_Buffer controlled_buffer_3
  assign CFFBUS[1] = clFETCH ? 1'b1 : 1'bz;  // Controlled_Buffer controlled_buffer_4
  assign CFFBUS[2] = stADDR ? 1'b1 : 1'bz;  // Controlled_Buffer controlled_buffer_5
  assign CFFBUS[4] = stEXEC ? 1'b1 : 1'bz;  // Controlled_Buffer controlled_buffer_6
  assign CREGBUS[4] = ldIR7__0 ? 1'b1 : 1'bz;  // Controlled_Buffer controlled_buffer_7
  assign CREGBUS[5] = ldIR15__8 ? 1'b1 : 1'bz;  // Controlled_Buffer controlled_buffer_8
  assign CREGBUS[6] = ldIR23__16 ? 1'b1 : 1'bz;  // Controlled_Buffer controlled_buffer_9
  assign out_11 = rdMEM ? 1'b1 : 1'bz;  // Controlled_Buffer controlled_buffer_10

  // Other names for the same wires on the sheet: CLK = in_2; FCBUS = in_3; FETCH = in_4[0]; ADDR = in_4[1];
  //   EXEC = in_4[2]; INTR = in_4[3]; HALT = in_5[0]; RTS = in_5[1]; RTI = in_5[2]; JMP = in_5[3]; JSR = in_5[4];
  //   BLSS = in_5[5]; jmp2 = in_5[5]; JLEQ = in_5[6]; LD = in_5[7]; ST = in_5[8]; ADD = in_5[9]; SUB = in_5[10];
  //   immed = in_6[0]; memdir = in_6[1]; regdir = in_6[2]; regindpom = in_6[3]; PSWSTART = PSW[0]; rst = in_1

  // Notes on the sheet:
  //   Operaciona jedinica
  //   Kontrolna jedinica
endmodule

module RAM (
  input  [15:0] in_1,
  input  in_2,
  input  [7:0] in_3,
  input  in_4,
  input  in_5,
  input  in_6,
  output [7:0] out_7,
  output out_8
);

  wire and_1_out, and_2_out, CNT0, LDCNT, not_1_out, notCNT0, or_1_out, reg4_ld_sl_sr_1_p6, rsff_2_p4,
       rsff_2_p5, rsff_3_p4, sl;
  wire [3:0] CNT, LFSR;

  // RSFF rsff_1: pin names not known; wires that end beside it: 1'b0, in_2, in_6, sl
  or or_1 (or_1_out, in_4, in_5);
  // REG4_LD_SL_SR reg4_ld_sl_sr_1: pin names not known; wires that end beside it: 1'b0, 1'b0, in_2, 4'b1111, LFSR, reg4_ld_sl_sr_1_p6, sl, in_6
  // RisingEdge risingedge_1: pin names not known; wires that end beside it: or_1_out, in_2, LDCNT
  // MEM64Kx8 mem64kx8_1: pin names not known; wires that end beside it: in_1, 1'b1, in_2, in_3, out_7, in_4
  xor xor_1 (reg4_ld_sl_sr_1_p6, LFSR[2], LFSR[3]);
  and and_1 (and_1_out, CNT0, not_1_out);
  not not_1 (not_1_out, LDCNT);
  // RSFF rsff_2: pin names not known; wires that end beside it: and_1_out, in_2, LDCNT, rsff_2_p4, rsff_2_p5
  not not_2 (rsff_2_p4, in_6);
  and and_2 (and_2_out, rsff_2_p5, CNT0);
  // REG4m_DEC_LD reg4m_dec_ld_1: pin names not known; wires that end beside it: in_2, LFSR, CNT, LDCNT, notCNT0, notCNT0
  or or_2 (notCNT0, CNT[0], CNT[1], CNT[2], CNT[3]);
  // RSFF rsff_3: pin names not known; wires that end beside it: out_8, in_2, and_2_out, rsff_3_p4, out_8
  not not_3 (rsff_3_p4, in_6);
  not not_4 (CNT0, notCNT0);

  // Other names for the same wires on the sheet: ADR[15:0] = in_1; CLK = in_2; DIN[7:0] = in_3; DOUT[7:0] = out_7;
  //   fc = out_8; RDMEM = in_5; rst = in_6; WRMEM = in_4

  // Notes on the sheet:
  //   Random broj predstavlja vreme pristupa memoriji
  //   Brojac za generisanje random broja 
  //   Jedinica za generisanje function complete (fc) signala
  //   Brojac za dekrementiranje random broja
endmodule
